// Digital circuit I-mem.dig as structural Verilog
module I_mem (
  input  [15:0] INST,
  input  I_mem,
  input  [15:0] OUT1,
  output [15:0] A
);

  Multiplexer #(.Bits(16)) multiplexer_1 (.sel(I_mem), .in_0(OUT1), .in_1({{8{1'b0}}, INST[7:0]}), .out(A));
endmodule

/* Test case:
I-mem	OUT1	INST	A
let ldiop = 0b0010;

loop(i, 100)
    let o = random(1<<16);
    let ra = random(1<<4);
    let imm = random(1<<8);
    (0) (o) (ldiop<<12 | ra<<8 | imm) (o)
    (1) (o) (ldiop<<12 | ra<<8 | imm) (0<<8 | imm)
end loop
*/
