// Digital circuit control_unit.dig as structural Verilog
module control_unit (
  input  [15:0] INST,
  input  Z,
  output [1:0] DMUX,
  output [1:0] ALUOP,
  output [2:0] RS1,
  output [2:0] RS2,
  output [2:0] WS,
  output WE,
  output EXEC,
  output SETH,
  output FLEN,
  output STR,
  output LDR,
  output LDI
);

  wire and_1_out, and_4_out, and_5_out, and_6_out, and_7_out, and_8_out, and_9_out, not_1_out, not_2_out,
       not_3_out, not_4_out, not_5_out, not_6_out, not_7_out, not_8_out, not_9_out, not_10_out, not_12_out,
       not_13_out, or_1_out;

  not not_1 (not_1_out, INST[15]);
  not not_2 (not_2_out, INST[14]);
  not not_3 (not_3_out, INST[13]);
  and and_1 (and_1_out, INST[12], not_3_out, not_2_out, not_1_out);
  Multiplexer #(.Selector_Bits(4)) multiplexer_1 (
    .sel(INST[15:12]), .in_0(1'b0), .in_1(1'b1), .in_2(1'b1), .in_3(1'b1), .in_4(1'b1), .in_5(1'b1),
    .in_6(1'b1), .in_7(1'b1), .in_8(1'b0), .in_9(1'b0), .in_10(1'b0), .in_11(1'b0), .in_12(1'b1),
    .in_13(1'b1), .in_14(1'b1), .in_15(1'b1), .out(DMUX[0]));
  Multiplexer #(.Selector_Bits(4)) multiplexer_2 (
    .sel(INST[15:12]), .in_0(1'b1), .in_1(1'b1), .in_2(1'b0), .in_3(1'b1), .in_4(1'b1), .in_5(1'b0),
    .in_6(1'b1), .in_7(1'b1), .in_8(1'b0), .in_9(1'b0), .in_10(1'b0), .in_11(1'b0), .in_12(1'b1),
    .in_13(1'b1), .in_14(1'b1), .in_15(1'b1), .out(DMUX[1]));
  and and_2 (ALUOP[1], INST[13], INST[15]);
  and and_3 (ALUOP[0], INST[12], INST[15]);
  not not_4 (not_4_out, Z);
  and and_4 (and_4_out, not_4_out, INST[11]);
  not not_5 (not_5_out, INST[13]);
  not not_6 (not_6_out, INST[15]);
  and and_5 (and_5_out, not_5_out, INST[14], not_6_out);
  not not_7 (not_7_out, INST[12]);
  not not_8 (not_8_out, INST[12]);
  not not_9 (not_9_out, INST[14]);
  not not_10 (not_10_out, INST[15]);
  not not_11 (EXEC, and_4_out);
  and and_6 (and_6_out, INST[12], and_5_out);
  and and_7 (and_7_out, and_5_out, not_7_out);
  and and_8 (and_8_out, not_12_out, INST[15]);
  not not_12 (not_12_out, INST[14]);
  and and_9 (and_9_out, not_8_out, INST[13], not_9_out, not_10_out);
  Multiplexer #(.Bits(3)) multiplexer_3 (.sel(and_7_out), .in_0(INST[2:0]), .in_1(INST[10:8]), .out(RS2));
  not not_13 (not_13_out, and_7_out);
  or or_1 (or_1_out, and_6_out, and_9_out);
  and and_10 (LDR, EXEC, or_1_out);
  and and_11 (STR, EXEC, and_7_out);
  and and_12 (WE, EXEC, not_13_out);
  and and_13 (FLEN, EXEC, and_8_out);
  and and_14 (SETH, EXEC, and_1_out);
  and and_15 (LDI, EXEC, and_9_out);

  assign RS1 = INST[6:4];
  assign WS = INST[10:8];

  // Other names for the same wires on the sheet: IN12 = INST[12]; IN13 = INST[13]; IN14 = INST[14]; IN15 = INST[15]

  // Notes on the sheet:
  //   z
  //   Rd
  //   Ra
  //   Rb
  //   opcode
endmodule

/* Test case All Tests:
	INST                                    WE  ALUOP  RS1   RS2  WS  STR  LDR DMUX

let aluop  = 0b1000;
let ldrop  = 0b0101;
let strop  = 0b0100;
let movlop = 0b0000;

loop(rd, 1<<3)
loop(ra, 1<<3)
loop(rb, 1<<3)

loop(i, 4)
	((aluop+i)<<12 | rd<<8 | ra<<4 | rb<<0) 1  (i)     (ra)  (rb) (rd)  0   X    0  #test add/sub/and/orr
end loop

	(ldrop    <<12 | rd<<8 | ra<<4 )        1  X       (ra)  x    (rd)  0   1    1  #test ldr
	(strop    <<12 | rd<<8 | ra<<4 )        0  X       (ra)  (rd)  X    1   X    X  #test str
	
	let imm = random(256);
	(movlop   <<12 | rd<<8 | imm )          1  X       X      X   (rd)  0   X    2  #test movl

end loop
end loop
end loop
*/

/* Test case EXEC:
	Z    INST    EXEC
loop(i, 100)
    let x = random(1<<4);
    let y = random(1<<11);
    (1) (x<<12 | 0<<11 | y) (1)
    (0) (x<<12 | 0<<11 | y) (1)
    (1) (x<<12 | 1<<11 | y) (1)
    (0) (x<<12 | 1<<11 | y) (0)
end loop
*/

/* Test case WS:
	INST                                    WS 

let aluop  = 0b1000;
let ldrop  = 0b0101;
let strop  = 0b0100;
let movlop = 0b0000;
let sethop = 0b0001;
let ldiop = 0b0010;

loop(rd, 1<<3)
loop(ra, 1<<3)
loop(rb, 1<<3)

loop(i, 4)
	((aluop+i)<<12 | rd<<8 | ra<<4 | rb<<0) (rd)  #test add/sub/and/orr
end loop

	(ldrop    <<12 | rd<<8 | ra<<4 )        (rd)   #test ldr
	(strop    <<12 | rd<<8 | ra<<4 )        X     #test str
	
	let imm = random(256);
	(movlop   <<12 | rd<<8 | imm )          (rd)  #test movl
	(sethop   <<12 | rd<<8 | imm )          (rd)  #test seth
	(ldiop    <<12 | rd<<8 | imm )          (rd)  #test ldi
end loop
end loop
end loop
*/

/* Test case RS1:
	INST                                    RS1  

let aluop  = 0b1000;
let ldrop  = 0b0101;
let strop  = 0b0100;
let movlop = 0b0000;

loop(rd, 1<<3)
loop(ra, 1<<3)
loop(rb, 1<<3)

loop(i, 4)
	((aluop+i)<<12 | rd<<8 | ra<<4 | rb<<0) (ra)  #test add/sub/and/orr
end loop

	(ldrop    <<12 | rd<<8 | ra<<4 )        (ra)  #test ldr
	(strop    <<12 | rd<<8 | ra<<4 )        (ra)  #test str

end loop
end loop
end loop
*/

/* Test case RS2:
	INST                                    RS2  

let aluop  = 0b1000;
let ldrop  = 0b0101;
let strop  = 0b0100;
let movlop = 0b0000;

loop(rd, 1<<3)
loop(ra, 1<<3)
loop(rb, 1<<3)

loop(i, 4)
	((aluop+i)<<12 | rd<<8 | ra<<4 | rb<<0) (rb) #test add/sub/and/orr
end loop
	(strop    <<12 | rd<<8 | ra<<4 )        (rd) #test str

end loop
end loop
end loop
*/

/* Test case LDR:
Z	INST                                    LDR 

let aluop  = 0b1000;
let ldrop  = 0b0101;
let strop  = 0b0100;
let movlop = 0b0000;
let sethop = 0b0001;
let ldiop = 0b0010;

loop(rd, 1<<3)
loop(ra, 1<<3)
loop(rb, 1<<3)

loop(i, 4)
	(0)((aluop+i)<<12 | 0<<11 | rd<<8 | ra<<4 | rb<<0) 0    #test add/sub/and/orr
	(1)((aluop+i)<<12 | 0<<11 | rd<<8 | ra<<4 | rb<<0) 0    #test add/sub/and/orr
        (0)((aluop+i)<<12 | 1<<11 | rd<<8 | ra<<4 | rb<<0) 0    #test add/sub/and/orr
        (1)((aluop+i)<<12 | 1<<11 | rd<<8 | ra<<4 | rb<<0) 0    #test add/sub/and/orr
end loop

	(0)(ldrop    <<12 | 0<<11 | rd<<8 | ra<<4 )        1    #test ldr
	(1)(ldrop    <<12 | 0<<11 | rd<<8 | ra<<4 )        1    #test ldr
	(0)(ldrop    <<12 | 1<<11 | rd<<8 | ra<<4 )        0    #test ldr
	(1)(ldrop    <<12 | 1<<11 | rd<<8 | ra<<4 )        1    #test ldr
	(0)(strop    <<12 | 0<<11 | rd<<8 | ra<<4 )        0    #test str
	(1)(strop    <<12 | 0<<11 | rd<<8 | ra<<4 )        0    #test str
	(0)(strop    <<12 | 1<<11 | rd<<8 | ra<<4 )        0    #test str
	(1)(strop    <<12 | 1<<11 | rd<<8 | ra<<4 )        0    #test str
	let imm = random(256);
	(0)(movlop   <<12 | 0<<11 | rd<<8 | imm )          0    #test movl
	(1)(movlop   <<12 | 0<<11 | rd<<8 | imm )          0    #test movl
	(0)(movlop   <<12 | 1<<11 | rd<<8 | imm )          0    #test movl
	(1)(movlop   <<12 | 1<<11 | rd<<8 | imm )          0    #test movl
	(0)(sethop   <<12 | 0<<11 | rd<<8 | imm )          0    #test seth
	(1)(sethop   <<12 | 0<<11 | rd<<8 | imm )          0    #test seth
	(0)(sethop   <<12 | 1<<11 | rd<<8 | imm )          0    #test seth
	(1)(sethop   <<12 | 1<<11 | rd<<8 | imm )          0    #test seth
	(0)(ldiop   <<12 | 0<<11 | rd<<8 | imm )          1    #test ldi
	(1)(ldiop   <<12 | 0<<11 | rd<<8 | imm )          1    #test ldi
	(0)(ldiop   <<12 | 1<<11 | rd<<8 | imm )          0    #test ldi
	(1)(ldiop   <<12 | 1<<11 | rd<<8 | imm )          1    #test ldi
end loop
end loop
end loop
*/

/* Test case STR:
Z	INST                                    STR 

let aluop  = 0b1000;
let ldrop  = 0b0101;
let strop  = 0b0100;
let movlop = 0b0000;
let sethop = 0b0001;

loop(rd, 1<<3)
loop(ra, 1<<3)
loop(rb, 1<<3)

loop(i, 4)
	(0)((aluop+i)<<12 | 0<<11 | rd<<8 | ra<<4 | rb<<0) 0    #test add/sub/and/orr
	(1)((aluop+i)<<12 | 0<<11 | rd<<8 | ra<<4 | rb<<0) 0    #test add/sub/and/orr
        (0)((aluop+i)<<12 | 1<<11 | rd<<8 | ra<<4 | rb<<0) 0    #test add/sub/and/orr
        (1)((aluop+i)<<12 | 1<<11 | rd<<8 | ra<<4 | rb<<0) 0    #test add/sub/and/orr
end loop

	(0)(ldrop    <<12 | 0<<11 | rd<<8 | ra<<4 )        0    #test ldr
	(1)(ldrop    <<12 | 0<<11 | rd<<8 | ra<<4 )        0    #test ldr
	(0)(ldrop    <<12 | 1<<11 | rd<<8 | ra<<4 )        0    #test ldr
	(1)(ldrop    <<12 | 1<<11 | rd<<8 | ra<<4 )        0    #test ldr
	(0)(strop    <<12 | 0<<11 | rd<<8 | ra<<4 )        1    #test str
	(1)(strop    <<12 | 0<<11 | rd<<8 | ra<<4 )        1    #test str
	(0)(strop    <<12 | 1<<11 | rd<<8 | ra<<4 )        0    #test str
	(1)(strop    <<12 | 1<<11 | rd<<8 | ra<<4 )        1    #test str
	let imm = random(256);
	(0)(movlop   <<12 | 0<<11 | rd<<8 | imm )          0    #test movl
	(1)(movlop   <<12 | 0<<11 | rd<<8 | imm )          0    #test movl
	(0)(movlop   <<12 | 1<<11 | rd<<8 | imm )          0    #test movl
	(1)(movlop   <<12 | 1<<11 | rd<<8 | imm )          0    #test movl
	(0)(sethop   <<12 | 0<<11 | rd<<8 | imm )          0    #test seth
	(1)(sethop   <<12 | 0<<11 | rd<<8 | imm )          0    #test seth
	(0)(sethop   <<12 | 1<<11 | rd<<8 | imm )          0    #test seth
	(1)(sethop   <<12 | 1<<11 | rd<<8 | imm )          0    #test seth
end loop
end loop
end loop
*/

/* Test case WE:
Z	INST                                    WE 

let aluop  = 0b1000;
let ldrop  = 0b0101;
let strop  = 0b0100;
let movlop = 0b0000;
let sethop = 0b0001;
let ldiop = 0b0010;

loop(rd, 1<<3)
loop(ra, 1<<3)
loop(rb, 1<<3)

loop(i, 4)
	(0)((aluop+i)<<12 | 0<<11 | rd<<8 | ra<<4 | rb<<0) 1    #test add/sub/and/orr
	(1)((aluop+i)<<12 | 0<<11 | rd<<8 | ra<<4 | rb<<0) 1    #test add/sub/and/orr
        (0)((aluop+i)<<12 | 1<<11 | rd<<8 | ra<<4 | rb<<0) 0    #test add/sub/and/orr
        (1)((aluop+i)<<12 | 1<<11 | rd<<8 | ra<<4 | rb<<0) 1    #test add/sub/and/orr
end loop

	(0)(ldrop    <<12 | 0<<11 | rd<<8 | ra<<4 )        1    #test ldr
	(1)(ldrop    <<12 | 0<<11 | rd<<8 | ra<<4 )        1    #test ldr
	(0)(ldrop    <<12 | 1<<11 | rd<<8 | ra<<4 )        0    #test ldr
	(1)(ldrop    <<12 | 1<<11 | rd<<8 | ra<<4 )        1    #test ldr
	(0)(strop    <<12 | 0<<11 | rd<<8 | ra<<4 )        0    #test str
	(1)(strop    <<12 | 0<<11 | rd<<8 | ra<<4 )        0    #test str
	(0)(strop    <<12 | 1<<11 | rd<<8 | ra<<4 )        0    #test str
	(1)(strop    <<12 | 1<<11 | rd<<8 | ra<<4 )        0    #test str
	let imm = random(256);
	(0)(movlop   <<12 | 0<<11 | rd<<8 | imm )          1    #test movl
	(1)(movlop   <<12 | 0<<11 | rd<<8 | imm )          1    #test movl
	(0)(movlop   <<12 | 1<<11 | rd<<8 | imm )          0    #test movl
	(1)(movlop   <<12 | 1<<11 | rd<<8 | imm )          1    #test movl
	(0)(sethop   <<12 | 0<<11 | rd<<8 | imm )          1    #test seth
	(1)(sethop   <<12 | 0<<11 | rd<<8 | imm )          1    #test seth
	(0)(sethop   <<12 | 1<<11 | rd<<8 | imm )          0    #test seth
	(1)(sethop   <<12 | 1<<11 | rd<<8 | imm )          1    #test seth
	(0)(ldiop   <<12 | 0<<11 | rd<<8 | imm )          1    #test ldi
	(1)(ldiop   <<12 | 0<<11 | rd<<8 | imm )          1    #test ldi
	(0)(ldiop   <<12 | 1<<11 | rd<<8 | imm )          0    #test ldi
	(1)(ldiop   <<12 | 1<<11 | rd<<8 | imm )          1    #test ldi
end loop
end loop
end loop
*/

/* Test case ALUOP:
	INST                                    ALUOP 

let aluop  = 0b1000;
let ldrop  = 0b0101;
let strop  = 0b0100;
let movlop = 0b0000;

loop(rd, 1<<3)
loop(ra, 1<<3)
loop(rb, 1<<3)

loop(i, 4)
	((aluop+i)<<12 | rd<<8 | ra<<4 | rb<<0) (i)    #test add/sub/and/orr
end loop

end loop
end loop
end loop
*/

/* Test case FLEN:
Z	INST                                    FLEN 

let aluop  = 0b1000;
let ldrop  = 0b0101;
let strop  = 0b0100;
let movlop = 0b0000;
let sethop = 0b0001;

loop(rd, 1<<3)
loop(ra, 1<<3)
loop(rb, 1<<3)

loop(i, 4)
	(0)((aluop+i)<<12 | 0<<11 | rd<<8 | ra<<4 | rb<<0) 1    #test add/sub/and/orr
	(1)((aluop+i)<<12 | 0<<11 | rd<<8 | ra<<4 | rb<<0) 1    #test add/sub/and/orr
        (0)((aluop+i)<<12 | 1<<11 | rd<<8 | ra<<4 | rb<<0) 0    #test add/sub/and/orr
        (1)((aluop+i)<<12 | 1<<11 | rd<<8 | ra<<4 | rb<<0) 1    #test add/sub/and/orr
end loop

	(0)(ldrop    <<12 | 0<<11 | rd<<8 | ra<<4 )        0    #test ldr
	(1)(ldrop    <<12 | 0<<11 | rd<<8 | ra<<4 )        0    #test ldr
	(0)(ldrop    <<12 | 1<<11 | rd<<8 | ra<<4 )        0    #test ldr
	(1)(ldrop    <<12 | 1<<11 | rd<<8 | ra<<4 )        0    #test ldr
	(0)(strop    <<12 | 0<<11 | rd<<8 | ra<<4 )        0    #test str
	(1)(strop    <<12 | 0<<11 | rd<<8 | ra<<4 )        0    #test str
	(0)(strop    <<12 | 1<<11 | rd<<8 | ra<<4 )        0    #test str
	(1)(strop    <<12 | 1<<11 | rd<<8 | ra<<4 )        0    #test str
	let imm = random(256);
	(0)(movlop   <<12 | 0<<11 | rd<<8 | imm )          0    #test movl
	(1)(movlop   <<12 | 0<<11 | rd<<8 | imm )          0    #test movl
	(0)(movlop   <<12 | 1<<11 | rd<<8 | imm )          0    #test movl
	(1)(movlop   <<12 | 1<<11 | rd<<8 | imm )          0    #test movl
	(0)(sethop   <<12 | 0<<11 | rd<<8 | imm )          0    #test seth
	(1)(sethop   <<12 | 0<<11 | rd<<8 | imm )          0    #test seth
	(0)(sethop   <<12 | 1<<11 | rd<<8 | imm )          0    #test seth
	(1)(sethop   <<12 | 1<<11 | rd<<8 | imm )          0    #test seth
end loop
end loop
end loop
*/

/* Test case SETH:
Z	INST                                    SETH 

let aluop  = 0b1000;
let ldrop  = 0b0101;
let strop  = 0b0100;
let movlop = 0b0000;
let sethop = 0b0001;

loop(rd, 1<<3)
loop(ra, 1<<3)
loop(rb, 1<<3)

loop(i, 4)
	(0)((aluop+i)<<12 | 0<<11 | rd<<8 | ra<<4 | rb<<0) 0    #test add/sub/and/orr
	(1)((aluop+i)<<12 | 0<<11 | rd<<8 | ra<<4 | rb<<0) 0    #test add/sub/and/orr
        (0)((aluop+i)<<12 | 1<<11 | rd<<8 | ra<<4 | rb<<0) 0    #test add/sub/and/orr
        (1)((aluop+i)<<12 | 1<<11 | rd<<8 | ra<<4 | rb<<0) 0    #test add/sub/and/orr
end loop

	(0)(ldrop    <<12 | 0<<11 | rd<<8 | ra<<4 )        0    #test ldr
	(1)(ldrop    <<12 | 0<<11 | rd<<8 | ra<<4 )        0    #test ldr
	(0)(ldrop    <<12 | 1<<11 | rd<<8 | ra<<4 )        0    #test ldr
	(1)(ldrop    <<12 | 1<<11 | rd<<8 | ra<<4 )        0    #test ldr
	(0)(strop    <<12 | 0<<11 | rd<<8 | ra<<4 )        0    #test str
	(1)(strop    <<12 | 0<<11 | rd<<8 | ra<<4 )        0    #test str
	(0)(strop    <<12 | 1<<11 | rd<<8 | ra<<4 )        0    #test str
	(1)(strop    <<12 | 1<<11 | rd<<8 | ra<<4 )        0    #test str
	let imm = random(256);
	(0)(movlop   <<12 | 0<<11 | rd<<8 | imm )          0    #test movl
	(1)(movlop   <<12 | 0<<11 | rd<<8 | imm )          0    #test movl
	(0)(movlop   <<12 | 1<<11 | rd<<8 | imm )          0    #test movl
	(1)(movlop   <<12 | 1<<11 | rd<<8 | imm )          0    #test movl
	(0)(sethop   <<12 | 0<<11 | rd<<8 | imm )          1    #test seth
	(1)(sethop   <<12 | 0<<11 | rd<<8 | imm )          1    #test seth
	(0)(sethop   <<12 | 1<<11 | rd<<8 | imm )          0    #test seth
	(1)(sethop   <<12 | 1<<11 | rd<<8 | imm )          1    #test seth
end loop
end loop
end loop
*/

/* Test case DMUX:
	INST                                    DMUX

let aluop  = 0b1000;
let ldrop  = 0b0101;
let strop  = 0b0100;
let movlop = 0b0000;
let sethop = 0b0001;
let ldiop = 0b0010;

loop(rd, 1<<3)
loop(ra, 1<<3)
loop(rb, 1<<3)

loop(i, 4)
	((aluop+i)<<12 | rd<<8 | ra<<4 | rb<<0) 0  #test add/sub/and/orr
end loop

	(ldrop    <<12 | rd<<8 | ra<<4 )        1  #test ldr
	(strop    <<12 | rd<<8 | ra<<4 )        3  #test str

	let imm = random(256);
	(movlop   <<12 | rd<<8 | imm )          2  #test movl
	(sethop   <<12 | rd<<8 | imm )          3  #test seth
	(ldiop    <<12 | rd<<8 | imm )          1  #test ldi
end loop
end loop
end loop
*/

/* Test case LDI:
Z	INST                                    LDI 

let aluop  = 0b1000;
let ldrop  = 0b0101;
let strop  = 0b0100;
let movlop = 0b0000;
let sethop = 0b0001;
let ldiop = 0b0010;

loop(rd, 1<<3)
loop(ra, 1<<3)
loop(rb, 1<<3)

loop(i, 4)
	(0)((aluop+i)<<12 | 0<<11 | rd<<8 | ra<<4 | rb<<0) 0    #test add/sub/and/orr
	(1)((aluop+i)<<12 | 0<<11 | rd<<8 | ra<<4 | rb<<0) 0    #test add/sub/and/orr
        (0)((aluop+i)<<12 | 1<<11 | rd<<8 | ra<<4 | rb<<0) 0    #test add/sub/and/orr
        (1)((aluop+i)<<12 | 1<<11 | rd<<8 | ra<<4 | rb<<0) 0    #test add/sub/and/orr
end loop

	(0)(ldrop    <<12 | 0<<11 | rd<<8 | ra<<4 )        0    #test ldr
	(1)(ldrop    <<12 | 0<<11 | rd<<8 | ra<<4 )        0    #test ldr
	(0)(ldrop    <<12 | 1<<11 | rd<<8 | ra<<4 )        0    #test ldr
	(1)(ldrop    <<12 | 1<<11 | rd<<8 | ra<<4 )        0    #test ldr
	(0)(strop    <<12 | 0<<11 | rd<<8 | ra<<4 )        0    #test str
	(1)(strop    <<12 | 0<<11 | rd<<8 | ra<<4 )        0    #test str
	(0)(strop    <<12 | 1<<11 | rd<<8 | ra<<4 )        0    #test str
	(1)(strop    <<12 | 1<<11 | rd<<8 | ra<<4 )        0    #test str
	let imm = random(256);
	(0)(movlop   <<12 | 0<<11 | rd<<8 | imm )          0    #test movl
	(1)(movlop   <<12 | 0<<11 | rd<<8 | imm )          0    #test movl
	(0)(movlop   <<12 | 1<<11 | rd<<8 | imm )          0    #test movl
	(1)(movlop   <<12 | 1<<11 | rd<<8 | imm )          0    #test movl
	(0)(sethop   <<12 | 0<<11 | rd<<8 | imm )          0    #test seth
	(1)(sethop   <<12 | 0<<11 | rd<<8 | imm )          0    #test seth
	(0)(sethop   <<12 | 1<<11 | rd<<8 | imm )          0    #test seth
	(1)(sethop   <<12 | 1<<11 | rd<<8 | imm )          0    #test seth
	(0)(ldiop   <<12 | 0<<11 | rd<<8 | imm )          1    #test ldi
	(1)(ldiop   <<12 | 0<<11 | rd<<8 | imm )          1    #test ldi
	(0)(ldiop   <<12 | 1<<11 | rd<<8 | imm )          0    #test ldi
	(1)(ldiop   <<12 | 1<<11 | rd<<8 | imm )          1    #test ldi
end loop
end loop
end loop
*/
