// Digital circuit control_unit2.dig as structural Verilog
module control_unit2 (
  input  [15:0] INST,
  input  Z,
  output [1:0] DMUX,
  output [1:0] ALUOP,
  output [2:0] RS1,
  output [2:0] RS2,
  output [2:0] WS,
  output WE,
  output EXEC,
  output SETH,
  output FLEN,
  output STR,
  output LDR,
  output I_mem
);

  wire ALU, demultiplexer_1_out_8, demultiplexer_1_out_9, demultiplexer_1_out_10, demultiplexer_1_out_11,
       LDI, LDR_t, MOVL, not_1_out, or_2_out, or_3_out, or_4_out, or_5_out, SETH_t, STI, STR_t;

  Demultiplexer #(.Selector_Bits(4)) demultiplexer_1 (
    .sel(INST[15:12]), .in(1'b1), .out_0(MOVL), .out_1(SETH_t), .out_2(STI), .out_3(LDI), .out_4(STR_t),
    .out_5(LDR_t), .out_8(demultiplexer_1_out_8), .out_9(demultiplexer_1_out_9),
    .out_10(demultiplexer_1_out_10), .out_11(demultiplexer_1_out_11));  // open: out_6, out_7, out_12, out_13, out_14, out_15
  or or_1 (ALU, demultiplexer_1_out_8, demultiplexer_1_out_9, demultiplexer_1_out_10, demultiplexer_1_out_11);
  not not_1 (not_1_out, Z);
  Multiplexer #(.Bits(3)) multiplexer_1 (.sel(ALU), .in_0(INST[10:8]), .in_1(INST[2:0]), .out(RS2));
  nand nand_1 (EXEC, not_1_out, INST[11]);
  or or_2 (or_2_out, LDI, LDR_t);
  or or_3 (or_3_out, STI, STR_t);
  or or_4 (or_4_out, MOVL, SETH_t, LDI, LDR_t, ALU);
  nor nor_1 (DMUX[0], MOVL, ALU);
  nor nor_2 (DMUX[1], LDI, LDR_t, ALU);
  or or_5 (or_5_out, STI, LDI);
  and and_1 (LDR, EXEC, or_2_out);
  and and_2 (STR, EXEC, or_3_out);
  and and_3 (WE, EXEC, or_4_out);
  and and_4 (FLEN, EXEC, ALU);
  and and_5 (SETH, EXEC, SETH_t);
  and and_6 (I_mem, EXEC, or_5_out);

  assign ALUOP = INST[13:12];
  assign RS1 = INST[6:4];
  assign WS = INST[10:8];

  // Other names for the same wires on the sheet: _12_13[1:0] = INST[13:12]

  // Notes on the sheet:
  //   z
  //   Rd
  //   Ra
  //   Rb
  //   opcode
endmodule

/* Test case All Tests:
	INST                                    WE  ALUOP  RS1   RS2  WS  STR  LDR DMUX

let aluop  = 0b1000;
let ldrop  = 0b0101;
let strop  = 0b0100;
let movlop = 0b0000;
let sethop = 0b0001;
let stiop = 0b0010;
let ldiop = 0b0011;

loop(rd, 1<<3)
loop(ra, 1<<3)
loop(rb, 1<<3)

loop(i, 4)
	((aluop+i)<<12 | rd<<8 | ra<<4 | rb<<0) 1  (i)     (ra)  (rb) (rd)  0   0    0  #test add/sub/and/orr
end loop

	(ldrop    <<12 | rd<<8 | ra<<4 )        1  X       (ra)   X   (rd)  0   1    1  #test ldr
	(strop    <<12 | rd<<8 | ra<<4 )        0  X       (ra)  (rd)  X    1   0    3  #test str
	
	let imm = random(256);
	(movlop   <<12 | rd<<8 | imm )          1  X       X      X   (rd)  0   0    2  #test movl
	(sethop   <<12 | rd<<8 | imm )          1  X       X      X   (rd)  0   0    3  #test seth
	(stiop    <<12 | rd<<8 | imm )          0  X       X     (rd)  X    1   0    3  #test sti
	(ldiop    <<12 | rd<<8 | imm )          1  X       X      X   (rd)  0   1    1  #test sti
end loop
end loop
end loop
*/

/* Test case EXEC:
	Z    INST    EXEC
loop(i, 100)
    let x = random(1<<4);
    let y = random(1<<11);
    (1) (x<<12 | 0<<11 | y) (1)
    (0) (x<<12 | 0<<11 | y) (1)
    (1) (x<<12 | 1<<11 | y) (1)
    (0) (x<<12 | 1<<11 | y) (0)
end loop
*/

/* Test case WS:
	INST                                    WS 

let aluop  = 0b1000;
let ldrop  = 0b0101;
let strop  = 0b0100;
let movlop = 0b0000;
let sethop = 0b0001;
let stiop = 0b0010;
let ldiop = 0b0011;

loop(rd, 1<<3)
loop(ra, 1<<3)
loop(rb, 1<<3)

loop(i, 4)
	((aluop+i)<<12 | rd<<8 | ra<<4 | rb<<0) (rd)  #test add/sub/and/orr
end loop

	(ldrop    <<12 | rd<<8 | ra<<4 )        (rd)   #test ldr
	(strop    <<12 | rd<<8 | ra<<4 )        X     #test str
	
	let imm = random(256);
	(movlop   <<12 | rd<<8 | imm )          (rd)  #test movl
	(sethop   <<12 | rd<<8 | imm )          (rd)  #test seth
	(stiop    <<12 | rd<<8 | imm )          (rd)  #test sti
	(ldiop    <<12 | rd<<8 | imm )          (rd)  #test ldi
end loop
end loop
end loop
*/

/* Test case RS1:
	INST                                    RS1  

let aluop  = 0b1000;
let ldrop  = 0b0101;
let strop  = 0b0100;
let movlop = 0b0000;

loop(rd, 1<<3)
loop(ra, 1<<3)
loop(rb, 1<<3)

loop(i, 4)
	((aluop+i)<<12 | rd<<8 | ra<<4 | rb<<0) (ra)  #test add/sub/and/orr
end loop

	(ldrop    <<12 | rd<<8 | ra<<4 )        (ra)  #test ldr
	(strop    <<12 | rd<<8 | ra<<4 )        (ra)  #test str

end loop
end loop
end loop
*/

/* Test case RS2:
	INST                                    RS2  

let aluop  = 0b1000;
let ldrop  = 0b0101;
let strop  = 0b0100;
let movlop = 0b0000;
let sethop = 0b0001;
let stiop = 0b0010;
let ldiop = 0b0011;

loop(rd, 1<<3)
loop(ra, 1<<3)
loop(rb, 1<<3)

loop(i, 4)
	((aluop+i)<<12 | rd<<8 | ra<<4 | rb<<0) (rb) #test add/sub/and/orr
end loop
	(ldrop    <<12 | rd<<8 | ra<<4 )        (rd) #test ldr
	(strop    <<12 | rd<<8 | ra<<4 )        (rd) #test str
	let imm = random(1<<8);
	(movlop   <<12 | rd<<8 |imm)		(rd) #test movl
	(sethop   <<12 | rd<<8 |imm)		(rd) #test seth
	(stiop    <<12 | rd<<8 |imm)		(rd) #test sti
	(ldiop    <<12 | rd<<8 |imm)		(rd) #test ldi
end loop
end loop
end loop
*/

/* Test case LDR:
Z	INST                                    LDR 

let aluop  = 0b1000;
let ldrop  = 0b0101;
let strop  = 0b0100;
let movlop = 0b0000;
let sethop = 0b0001;
let stiop = 0b0010;
let ldiop = 0b0011;

loop(rd, 1<<3)
loop(ra, 1<<3)
loop(rb, 1<<3)

loop(i, 4)
	(0)((aluop+i)<<12 | 0<<11 | rd<<8 | ra<<4 | rb<<0) 0    #test add/sub/and/orr
	(1)((aluop+i)<<12 | 0<<11 | rd<<8 | ra<<4 | rb<<0) 0    #test add/sub/and/orr
        (0)((aluop+i)<<12 | 1<<11 | rd<<8 | ra<<4 | rb<<0) 0    #test add/sub/and/orr
        (1)((aluop+i)<<12 | 1<<11 | rd<<8 | ra<<4 | rb<<0) 0    #test add/sub/and/orr
end loop

	(0)(ldrop    <<12 | 0<<11 | rd<<8 | ra<<4 )        1    #test ldr
	(1)(ldrop    <<12 | 0<<11 | rd<<8 | ra<<4 )        1    #test ldr
	(0)(ldrop    <<12 | 1<<11 | rd<<8 | ra<<4 )        0    #test ldr
	(1)(ldrop    <<12 | 1<<11 | rd<<8 | ra<<4 )        1    #test ldr
	(0)(strop    <<12 | 0<<11 | rd<<8 | ra<<4 )        0    #test str
	(1)(strop    <<12 | 0<<11 | rd<<8 | ra<<4 )        0    #test str
	(0)(strop    <<12 | 1<<11 | rd<<8 | ra<<4 )        0    #test str
	(1)(strop    <<12 | 1<<11 | rd<<8 | ra<<4 )        0    #test str
	let imm = random(256);
	(0)(movlop   <<12 | 0<<11 | rd<<8 | imm )          0    #test movl
	(1)(movlop   <<12 | 0<<11 | rd<<8 | imm )          0    #test movl
	(0)(movlop   <<12 | 1<<11 | rd<<8 | imm )          0    #test movl
	(1)(movlop   <<12 | 1<<11 | rd<<8 | imm )          0    #test movl
	(0)(sethop   <<12 | 0<<11 | rd<<8 | imm )          0    #test seth
	(1)(sethop   <<12 | 0<<11 | rd<<8 | imm )          0    #test seth
	(0)(sethop   <<12 | 1<<11 | rd<<8 | imm )          0    #test seth
	(1)(sethop   <<12 | 1<<11 | rd<<8 | imm )          0    #test seth
	(0)(stiop    <<12 | 0<<11 | rd<<8 | imm )          0    #test sti
	(1)(stiop    <<12 | 0<<11 | rd<<8 | imm )          0    #test sti
	(0)(stiop    <<12 | 1<<11 | rd<<8 | imm )          0    #test sti
	(1)(stiop    <<12 | 1<<11 | rd<<8 | imm )          0    #test sti
	(0)(ldiop    <<12 | 0<<11 | rd<<8 | imm )          1    #test ldi
	(1)(ldiop    <<12 | 0<<11 | rd<<8 | imm )          1    #test ldi
	(0)(ldiop    <<12 | 1<<11 | rd<<8 | imm )          0    #test ldi
	(1)(ldiop    <<12 | 1<<11 | rd<<8 | imm )          1    #test ldi
end loop
end loop
end loop
*/

/* Test case STR:
Z	INST                                    STR 

let aluop  = 0b1000;
let ldrop  = 0b0101;
let strop  = 0b0100;
let movlop = 0b0000;
let sethop = 0b0001;
let stiop = 0b0010;
let ldiop = 0b0011;

loop(rd, 1<<3)
loop(ra, 1<<3)
loop(rb, 1<<3)

loop(i, 4)
	(0)((aluop+i)<<12 | 0<<11 | rd<<8 | ra<<4 | rb<<0) 0    #test add/sub/and/orr
	(1)((aluop+i)<<12 | 0<<11 | rd<<8 | ra<<4 | rb<<0) 0    #test add/sub/and/orr
        (0)((aluop+i)<<12 | 1<<11 | rd<<8 | ra<<4 | rb<<0) 0    #test add/sub/and/orr
        (1)((aluop+i)<<12 | 1<<11 | rd<<8 | ra<<4 | rb<<0) 0    #test add/sub/and/orr
end loop

	(0)(ldrop    <<12 | 0<<11 | rd<<8 | ra<<4 )        0    #test ldr
	(1)(ldrop    <<12 | 0<<11 | rd<<8 | ra<<4 )        0    #test ldr
	(0)(ldrop    <<12 | 1<<11 | rd<<8 | ra<<4 )        0    #test ldr
	(1)(ldrop    <<12 | 1<<11 | rd<<8 | ra<<4 )        0    #test ldr
	(0)(strop    <<12 | 0<<11 | rd<<8 | ra<<4 )        1    #test str
	(1)(strop    <<12 | 0<<11 | rd<<8 | ra<<4 )        1    #test str
	(0)(strop    <<12 | 1<<11 | rd<<8 | ra<<4 )        0    #test str
	(1)(strop    <<12 | 1<<11 | rd<<8 | ra<<4 )        1    #test str
	let imm = random(256);
	(0)(movlop   <<12 | 0<<11 | rd<<8 | imm )          0    #test movl
	(1)(movlop   <<12 | 0<<11 | rd<<8 | imm )          0    #test movl
	(0)(movlop   <<12 | 1<<11 | rd<<8 | imm )          0    #test movl
	(1)(movlop   <<12 | 1<<11 | rd<<8 | imm )          0    #test movl
	(0)(sethop   <<12 | 0<<11 | rd<<8 | imm )          0    #test seth
	(1)(sethop   <<12 | 0<<11 | rd<<8 | imm )          0    #test seth
	(0)(sethop   <<12 | 1<<11 | rd<<8 | imm )          0    #test seth
	(1)(sethop   <<12 | 1<<11 | rd<<8 | imm )          0    #test seth
	(0)(stiop    <<12 | 0<<11 | rd<<8 | imm )          1    #test sti
	(1)(stiop    <<12 | 0<<11 | rd<<8 | imm )          1    #test sti
	(0)(stiop    <<12 | 1<<11 | rd<<8 | imm )          0    #test sti
	(1)(stiop    <<12 | 1<<11 | rd<<8 | imm )          1    #test sti
	(0)(ldiop    <<12 | 0<<11 | rd<<8 | imm )          0    #test ldi
	(1)(ldiop    <<12 | 0<<11 | rd<<8 | imm )          0    #test ldi
	(0)(ldiop    <<12 | 1<<11 | rd<<8 | imm )          0    #test ldi
	(1)(ldiop    <<12 | 1<<11 | rd<<8 | imm )          0    #test ldi
end loop
end loop
end loop
*/

/* Test case WE:
Z	INST                                    WE 

let aluop  = 0b1000;
let ldrop  = 0b0101;
let strop  = 0b0100;
let movlop = 0b0000;
let sethop = 0b0001;
let stiop = 0b0010;
let ldiop = 0b0011;
let udop = 0b1111;

loop(rd, 1<<3)
loop(ra, 1<<3)
loop(rb, 1<<3)

loop(i, 4)
	(0)((aluop+i)<<12 | 0<<11 | rd<<8 | ra<<4 | rb<<0) 1    #test add/sub/and/orr
	(1)((aluop+i)<<12 | 0<<11 | rd<<8 | ra<<4 | rb<<0) 1    #test add/sub/and/orr
        (0)((aluop+i)<<12 | 1<<11 | rd<<8 | ra<<4 | rb<<0) 0    #test add/sub/and/orr
        (1)((aluop+i)<<12 | 1<<11 | rd<<8 | ra<<4 | rb<<0) 1    #test add/sub/and/orr
end loop

	(0)(ldrop    <<12 | 0<<11 | rd<<8 | ra<<4 )        1    #test ldr
	(1)(ldrop    <<12 | 0<<11 | rd<<8 | ra<<4 )        1    #test ldr
	(0)(ldrop    <<12 | 1<<11 | rd<<8 | ra<<4 )        0    #test ldr
	(1)(ldrop    <<12 | 1<<11 | rd<<8 | ra<<4 )        1    #test ldr
	(0)(strop    <<12 | 0<<11 | rd<<8 | ra<<4 )        0    #test str
	(1)(strop    <<12 | 0<<11 | rd<<8 | ra<<4 )        0    #test str
	(0)(strop    <<12 | 1<<11 | rd<<8 | ra<<4 )        0    #test str
	(1)(strop    <<12 | 1<<11 | rd<<8 | ra<<4 )        0    #test str
	let imm = random(256);
	(0)(movlop   <<12 | 0<<11 | rd<<8 | imm )          1    #test movl
	(1)(movlop   <<12 | 0<<11 | rd<<8 | imm )          1    #test movl
	(0)(movlop   <<12 | 1<<11 | rd<<8 | imm )          0    #test movl
	(1)(movlop   <<12 | 1<<11 | rd<<8 | imm )          1    #test movl
	(0)(sethop   <<12 | 0<<11 | rd<<8 | imm )          1    #test seth
	(1)(sethop   <<12 | 0<<11 | rd<<8 | imm )          1    #test seth
	(0)(sethop   <<12 | 1<<11 | rd<<8 | imm )          0    #test seth
	(1)(sethop   <<12 | 1<<11 | rd<<8 | imm )          1    #test seth
	(0)(stiop    <<12 | 0<<11 | rd<<8 | imm )          0    #test sti
	(1)(stiop    <<12 | 0<<11 | rd<<8 | imm )          0    #test sti
	(0)(stiop    <<12 | 1<<11 | rd<<8 | imm )          0    #test sti
	(1)(stiop    <<12 | 1<<11 | rd<<8 | imm )          0    #test sti
	(0)(ldiop    <<12 | 0<<11 | rd<<8 | imm )          1    #test ldi
	(1)(ldiop    <<12 | 0<<11 | rd<<8 | imm )          1    #test ldi
	(0)(ldiop    <<12 | 1<<11 | rd<<8 | imm )          0    #test ldi
	(1)(ldiop    <<12 | 1<<11 | rd<<8 | imm )          1    #test ldi
	(0)(udop     <<12 | 0<<11 | rd<<8 | imm )          0    #test undefined
	(1)(udop     <<12 | 0<<11 | rd<<8 | imm )          0    #test undefined
	(0)(udop     <<12 | 1<<11 | rd<<8 | imm )          0    #test undefined
	(1)(udop     <<12 | 1<<11 | rd<<8 | imm )          0    #test undefined
end loop
end loop
end loop
*/

/* Test case ALUOP:
	INST                                    ALUOP 

let aluop  = 0b1000;
let ldrop  = 0b0101;
let strop  = 0b0100;
let movlop = 0b0000;

loop(rd, 1<<3)
loop(ra, 1<<3)
loop(rb, 1<<3)

loop(i, 4)
	((aluop+i)<<12 | rd<<8 | ra<<4 | rb<<0) (i)    #test add/sub/and/orr
end loop

end loop
end loop
end loop
*/

/* Test case FLEN:
Z	INST                                    FLEN 

let aluop  = 0b1000;
let ldrop  = 0b0101;
let strop  = 0b0100;
let movlop = 0b0000;
let sethop = 0b0001;
let stiop = 0b0010;
let ldiop = 0b0011;
let udop = 0b1111;

loop(rd, 1<<3)
loop(ra, 1<<3)
loop(rb, 1<<3)

loop(i, 4)
	(0)((aluop+i)<<12 | 0<<11 | rd<<8 | ra<<4 | rb<<0) 1    #test add/sub/and/orr
	(1)((aluop+i)<<12 | 0<<11 | rd<<8 | ra<<4 | rb<<0) 1    #test add/sub/and/orr
        (0)((aluop+i)<<12 | 1<<11 | rd<<8 | ra<<4 | rb<<0) 0    #test add/sub/and/orr
        (1)((aluop+i)<<12 | 1<<11 | rd<<8 | ra<<4 | rb<<0) 1    #test add/sub/and/orr
end loop

	(0)(ldrop    <<12 | 0<<11 | rd<<8 | ra<<4 )        0    #test ldr
	(1)(ldrop    <<12 | 0<<11 | rd<<8 | ra<<4 )        0    #test ldr
	(0)(ldrop    <<12 | 1<<11 | rd<<8 | ra<<4 )        0    #test ldr
	(1)(ldrop    <<12 | 1<<11 | rd<<8 | ra<<4 )        0    #test ldr
	(0)(strop    <<12 | 0<<11 | rd<<8 | ra<<4 )        0    #test str
	(1)(strop    <<12 | 0<<11 | rd<<8 | ra<<4 )        0    #test str
	(0)(strop    <<12 | 1<<11 | rd<<8 | ra<<4 )        0    #test str
	(1)(strop    <<12 | 1<<11 | rd<<8 | ra<<4 )        0    #test str
	let imm = random(256);
	(0)(movlop   <<12 | 0<<11 | rd<<8 | imm )          0    #test movl
	(1)(movlop   <<12 | 0<<11 | rd<<8 | imm )          0    #test movl
	(0)(movlop   <<12 | 1<<11 | rd<<8 | imm )          0    #test movl
	(1)(movlop   <<12 | 1<<11 | rd<<8 | imm )          0    #test movl
	(0)(sethop   <<12 | 0<<11 | rd<<8 | imm )          0    #test seth
	(1)(sethop   <<12 | 0<<11 | rd<<8 | imm )          0    #test seth
	(0)(sethop   <<12 | 1<<11 | rd<<8 | imm )          0    #test seth
	(1)(sethop   <<12 | 1<<11 | rd<<8 | imm )          0    #test seth
	(0)(stiop    <<12 | 0<<11 | rd<<8 | imm )          0    #test sti
	(1)(stiop    <<12 | 0<<11 | rd<<8 | imm )          0    #test sti
	(0)(stiop    <<12 | 1<<11 | rd<<8 | imm )          0    #test sti
	(1)(stiop    <<12 | 1<<11 | rd<<8 | imm )          0    #test sti
	(0)(ldiop    <<12 | 0<<11 | rd<<8 | imm )          0    #test ldi
	(1)(ldiop    <<12 | 0<<11 | rd<<8 | imm )          0    #test ldi
	(0)(ldiop    <<12 | 1<<11 | rd<<8 | imm )          0    #test ldi
	(1)(ldiop    <<12 | 1<<11 | rd<<8 | imm )          0    #test ldi
	(0)(udop     <<12 | 0<<11 | rd<<8 | imm )          0    #test undefined
	(1)(udop     <<12 | 0<<11 | rd<<8 | imm )          0    #test undefined
	(0)(udop     <<12 | 1<<11 | rd<<8 | imm )          0    #test undefined
	(1)(udop     <<12 | 1<<11 | rd<<8 | imm )          0    #test undefined
end loop
end loop
end loop
*/

/* Test case SETH:
Z	INST                                    SETH 

let aluop  = 0b1000;
let ldrop  = 0b0101;
let strop  = 0b0100;
let movlop = 0b0000;
let sethop = 0b0001;
let stiop = 0b0010;
let ldiop = 0b0011;
let udop = 0b1111;

loop(rd, 1<<3)
loop(ra, 1<<3)
loop(rb, 1<<3)

loop(i, 4)
	(0)((aluop+i)<<12 | 0<<11 | rd<<8 | ra<<4 | rb<<0) 0    #test add/sub/and/orr
	(1)((aluop+i)<<12 | 0<<11 | rd<<8 | ra<<4 | rb<<0) 0    #test add/sub/and/orr
        (0)((aluop+i)<<12 | 1<<11 | rd<<8 | ra<<4 | rb<<0) 0    #test add/sub/and/orr
        (1)((aluop+i)<<12 | 1<<11 | rd<<8 | ra<<4 | rb<<0) 0    #test add/sub/and/orr
end loop

	(0)(ldrop    <<12 | 0<<11 | rd<<8 | ra<<4 )        0    #test ldr
	(1)(ldrop    <<12 | 0<<11 | rd<<8 | ra<<4 )        0    #test ldr
	(0)(ldrop    <<12 | 1<<11 | rd<<8 | ra<<4 )        0    #test ldr
	(1)(ldrop    <<12 | 1<<11 | rd<<8 | ra<<4 )        0    #test ldr
	(0)(strop    <<12 | 0<<11 | rd<<8 | ra<<4 )        0    #test str
	(1)(strop    <<12 | 0<<11 | rd<<8 | ra<<4 )        0    #test str
	(0)(strop    <<12 | 1<<11 | rd<<8 | ra<<4 )        0    #test str
	(1)(strop    <<12 | 1<<11 | rd<<8 | ra<<4 )        0    #test str
	let imm = random(256);
	(0)(movlop   <<12 | 0<<11 | rd<<8 | imm )          0    #test movl
	(1)(movlop   <<12 | 0<<11 | rd<<8 | imm )          0    #test movl
	(0)(movlop   <<12 | 1<<11 | rd<<8 | imm )          0    #test movl
	(1)(movlop   <<12 | 1<<11 | rd<<8 | imm )          0    #test movl
	(0)(sethop   <<12 | 0<<11 | rd<<8 | imm )          1    #test seth
	(1)(sethop   <<12 | 0<<11 | rd<<8 | imm )          1    #test seth
	(0)(sethop   <<12 | 1<<11 | rd<<8 | imm )          0    #test seth
	(1)(sethop   <<12 | 1<<11 | rd<<8 | imm )          1    #test seth
	(0)(stiop    <<12 | 0<<11 | rd<<8 | imm )          0    #test sti
	(1)(stiop    <<12 | 0<<11 | rd<<8 | imm )          0    #test sti
	(0)(stiop    <<12 | 1<<11 | rd<<8 | imm )          0    #test sti
	(1)(stiop    <<12 | 1<<11 | rd<<8 | imm )          0    #test sti
	(0)(ldiop    <<12 | 0<<11 | rd<<8 | imm )          0    #test ldi
	(1)(ldiop    <<12 | 0<<11 | rd<<8 | imm )          0    #test ldi
	(0)(ldiop    <<12 | 1<<11 | rd<<8 | imm )          0    #test ldi
	(1)(ldiop    <<12 | 1<<11 | rd<<8 | imm )          0    #test ldi
	(0)(udop     <<12 | 0<<11 | rd<<8 | imm )          0    #test undefined
	(1)(udop     <<12 | 0<<11 | rd<<8 | imm )          0    #test undefined
	(0)(udop     <<12 | 1<<11 | rd<<8 | imm )          0    #test undefined
	(1)(udop     <<12 | 1<<11 | rd<<8 | imm )          0    #test undefined
end loop
end loop
end loop
*/

/* Test case DMUX:
	INST                                    DMUX

let aluop  = 0b1000;
let ldrop  = 0b0101;
let strop  = 0b0100;
let movlop = 0b0000;
let sethop = 0b0001;
let stiop = 0b0010;
let ldiop = 0b0011;

loop(rd, 1<<3)
loop(ra, 1<<3)
loop(rb, 1<<3)

loop(i, 4)
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*/

/* Test case I-mem:
Z	INST                                    I-mem 

let aluop  = 0b1000;
let ldrop  = 0b0101;
let strop  = 0b0100;
let movlop = 0b0000;
let sethop = 0b0001;
let stiop = 0b0010;
let ldiop = 0b0011;

loop(rd, 1<<3)
loop(ra, 1<<3)
loop(rb, 1<<3)

loop(i, 4)
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*/
