// Digital circuit cpu.dig as structural Verilog
module cpu (
  input  CLK,
  output Z,
  output N,
  output C,
  output V
);

  wire control_unit_1_exec, control_unit_1_flen, control_unit_1_ldr, control_unit_1_seth, control_unit_1_str,
       control_unit_1_we;
  wire [1:0] control_unit_1_aluop, control_unit_1_dmux;
  wire [2:0] control_unit_1_rs1, control_unit_1_rs2, control_unit_1_ws;
  wire [7:0] RAM_d2;
  wire [15:0] alu_1_p5, fl_q, multiplexer_1_out, notconnected_1_out, RAM_d1, reg_file_1_out1,
       reg_file_1_out2, reg_file_1_pc;
  wire [15:8] RAM_d2_2;

  control_unit control_unit_1 (
    .INST({RAM_d2_2, RAM_d2}), .Z(fl_q[0]), .DMUX(control_unit_1_dmux), .ALUOP(control_unit_1_aluop),
    .RS1(control_unit_1_rs1), .RS2(control_unit_1_rs2), .WS(control_unit_1_ws), .WE(control_unit_1_we),
    .EXEC(control_unit_1_exec), .SETH(control_unit_1_seth), .FLEN(control_unit_1_flen),
    .STR(control_unit_1_str), .LDR(control_unit_1_ldr));
  Multiplexer #(.Selector_Bits(2), .Bits(16)) multiplexer_1 (
    .sel(control_unit_1_aluop), .in_0(alu_1_p5), .in_1(RAM_d1), .in_2({{8{1'b0}}, RAM_d2}),
    .in_3(notconnected_1_out), .out(multiplexer_1_out));
  // NotConnected on notconnected_1_out
  RAMDualAccess #(.AddrBits(16), .isProgramMemory("true"), .Bits(16)) RAM (
    .str(control_unit_1_str), .C(CLK), .ld(control_unit_1_ldr), .A1(reg_file_1_out1), .Din1(reg_file_1_pc),
    .A2(reg_file_1_out2), .D1(RAM_d1), .D2({RAM_d2_2, RAM_d2}));
  reg_file reg_file_1 (
    .IN(multiplexer_1_out), .clk(CLK), .RS1(control_unit_1_rs1), .RS2(control_unit_1_rs2),
    .WS(control_unit_1_ws), .WE(control_unit_1_we), .EXEC(control_unit_1_exec), .SETH(control_unit_1_seth),
    .FLIN(fl_q), .OUT1(reg_file_1_out1), .OUT2(reg_file_1_out2), .PC(reg_file_1_pc));
  // alu alu_1: pin names not known; wires that end beside it: reg_file_1_out1, reg_file_1_pc, control_unit_1_dmux, {V, C, N, Z}, alu_1_p5
  Register #(.Bits(16)) fl (.D({{12{1'b0}}, V, C, N, Z}), .C(CLK), .en(control_unit_1_flen), .Q(fl_q));
endmodule
